// Logisim project 8 Bit Adder.circ as structural Verilog: 1 circuit, main circuit main
module main (
  input  A7,
  input  A6,
  input  A5,
  input  A4,
  input  A3,
  input  A2,
  input  A1,
  input  A0,
  input  B7,
  input  B6,
  input  B5,
  input  B4,
  input  B3,
  input  B2,
  input  B1,
  input  B0,
  input  CI,
  output Overflow,
  output Sum7,
  output Sum6,
  output Sum5,
  output Sum4,
  output Sum3,
  output Sum2,
  output Sum1,
  output Sum0
);

  wire main_2_carry, main_3_carry, main_4_carry, main_5_carry, main_6_carry, main_7_carry, main_8_carry;

  FullAdder2_main main_1 (.Carry_in(main_2_carry), .A_in(A7), .B_in(B7), .Sum(Sum7), .Carry(Overflow));
  FullAdder2_main main_2 (.Carry_in(main_3_carry), .A_in(A6), .B_in(B6), .Sum(Sum6), .Carry(main_2_carry));
  FullAdder2_main main_3 (.Carry_in(main_4_carry), .A_in(A5), .B_in(B5), .Sum(Sum5), .Carry(main_3_carry));
  FullAdder2_main main_4 (.Carry_in(main_6_carry), .A_in(A4), .B_in(B4), .Sum(Sum4), .Carry(main_4_carry));
  FullAdder2_main main_5 (.Carry_in(main_7_carry), .A_in(A2), .B_in(B2), .Sum(Sum2), .Carry(main_5_carry));
  FullAdder2_main main_6 (.Carry_in(main_5_carry), .A_in(A3), .B_in(B3), .Sum(Sum3), .Carry(main_6_carry));
  FullAdder2_main main_7 (.Carry_in(main_8_carry), .A_in(A1), .B_in(B1), .Sum(Sum1), .Carry(main_7_carry));
  FullAdder2_main main_8 (.Carry_in(CI), .A_in(A0), .B_in(B0), .Sum(Sum0), .Carry(main_8_carry));

  // Notes on the sheet:
  //   8 Bit Adder
endmodule
