// Logisim project 8BitAdder.circ as structural Verilog: 1 circuit, main circuit main
// 8 bit adder
module main (
  input  A7,
  input  A6,
  input  A5,
  input  A4,
  input  A3,
  input  A2,
  input  A1,
  input  A0,
  input  B7,
  input  B6,
  input  B5,
  input  B4,
  input  B3,
  input  B2,
  input  B1,
  input  B0,
  input  CI,
  output CO,
  output S7,
  output S6,
  output S5,
  output S4,
  output S3,
  output S2,
  output S1,
  output S0
);

  wire main_2_overflow;

  _4BitAdder_main main_1 (
    .A3(A7), .B3(B7), .A2(A6), .B2(B6), .A1(A5), .B1(B5), .A0(A4), .B0(B4), .Overflow(CO), .Sum4(S7),
    .Sum3(S6), .Sum2(S5), .Sum1(S4), .CI(main_2_overflow));
  _4BitAdder_main main_2 (
    .A3(A3), .B3(B3), .A2(A2), .B2(B2), .A1(A1), .B1(B1), .A0(A0), .B0(B0), .Overflow(main_2_overflow),
    .Sum4(S3), .Sum3(S2), .Sum2(S1), .Sum1(S0), .CI(CI));
endmodule
