// Logisim project Adding Machine.circ as structural Verilog: 1 circuit, main circuit main
// Add Machine
module main (
  input  Clk,
  input  B7,
  input  B6,
  input  B5,
  input  B4,
  input  B3,
  input  B2,
  input  B1,
  input  B0,
  input  Sel,
  input  A7,
  input  A6,
  input  A5,
  input  A4,
  input  A3,
  input  A2,
  input  A1,
  input  A0,
  output out_19,
  output Out7,
  output Out6,
  output Out5,
  output Out4,
  output Out3,
  output Out2,
  output Out1,
  output Out0
);

  wire main_1_q0, main_1_q1, main_1_q2, main_1_q3, main_1_q4, main_1_q5, main_1_q6, main_1_q7, main_3_out0,
       main_3_out1, main_3_out2, main_3_out3, main_3_out4, main_3_out5, main_3_out6, main_3_out7;

  _8_bit_level_triggered_D_type_latch_main main_1 (
    .Clk(Clk), .D7(Out7), .D6(Out6), .D5(Out5), .D4(Out4), .D3(Out3), .D2(Out2), .D1(Out1), .D0(Out0),
    .Q7(main_1_q7), .Q6(main_1_q6), .Q5(main_1_q5), .Q4(main_1_q4), .Q3(main_1_q3), .Q2(main_1_q2),
    .Q1(main_1_q1), .Q0(main_1_q0));
  _8BitAdder_main main_2 (
    .CO(out_19), .A7(A7), .A6(A6), .A5(A5), .A4(A4), .A3(A3), .A2(A2), .A1(A1), .A0(A0), .B7(main_3_out7),
    .B6(main_3_out6), .B5(main_3_out5), .B4(main_3_out4), .B3(main_3_out3), .B2(main_3_out2),
    .B1(main_3_out1), .B0(main_3_out0), .S7(Out7), .S6(Out6), .S5(Out5), .S4(Out4), .S3(Out3), .S2(Out2),
    .S1(Out1), .S0(Out0), .CI(1'b0));
  _8_Bit_Selector_main main_3 (
    .A7(B7), .A6(B6), .A5(B5), .A4(B4), .A3(B3), .A2(B2), .A1(B1), .A0(B0), .B7(main_1_q7), .B6(main_1_q6),
    .B5(main_1_q5), .B4(main_1_q4), .B3(main_1_q3), .B2(main_1_q2), .B1(main_1_q1), .B0(main_1_q0),
    .Out7(main_3_out7), .Out6(main_3_out6), .Out5(main_3_out5), .Out4(main_3_out4), .Out3(main_3_out3),
    .Out2(main_3_out2), .Out1(main_3_out1), .Out0(main_3_out0), .Sel(Sel));

  // Notes on the sheet:
  //   Adding Machine
endmodule
