// Logisim project 8 Bit Selector.circ as structural Verilog: 1 circuit, main circuit main
// 8 Bit Selector
module main (
  input  A7,
  input  A6,
  input  A5,
  input  A4,
  input  A3,
  input  A2,
  input  A1,
  input  A0,
  input  B7,
  input  B6,
  input  B5,
  input  B4,
  input  B3,
  input  B2,
  input  B1,
  input  B0,
  input  Sel,
  output Out7,
  output Out6,
  output Out5,
  output Out4,
  output Out3,
  output Out2,
  output Out1,
  output Out0
);

  Selector_main main_1 (.B(B7), .Sel(Sel), .A(A7), .Out(Out7));
  Selector_main main_2 (.B(B6), .Sel(Sel), .A(A6), .Out(Out6));
  Selector_main main_3 (.B(B4), .Sel(Sel), .A(A4), .Out(Out4));
  Selector_main main_4 (.B(B5), .Sel(Sel), .A(A5), .Out(Out5));
  Selector_main main_5 (.B(B3), .Sel(Sel), .A(A3), .Out(Out3));
  Selector_main main_6 (.B(B2), .Sel(Sel), .A(A2), .Out(Out2));
  Selector_main main_7 (.B(B0), .Sel(Sel), .A(A0), .Out(Out0));
  Selector_main main_8 (.B(B1), .Sel(Sel), .A(A1), .Out(Out1));
endmodule
