// Logisim project Edge Triggered D Type Flip-Flop.circ as structural Verilog: 1 circuit, main circuit main
// Edge Flip-Flop
module main (
  input  Data,
  input  Clk,
  output Q,
  output Q_bar
);

  wire and_1_out, and_2_out, and_3_out, and_4_out, nor_1_out, nor_2_out, not_1_out, not_2_out;

  not not_1 (not_1_out, Clk);
  not not_2 (not_2_out, Data);
  and and_1 (and_1_out, Data, not_1_out);
  and and_2 (and_2_out, not_1_out, not_2_out);
  nor nor_1 (nor_1_out, and_1_out, nor_2_out);
  nor nor_2 (nor_2_out, nor_1_out, and_2_out);
  and and_3 (and_3_out, nor_1_out, Clk);
  and and_4 (and_4_out, Clk, nor_2_out);
  nor nor_3 (Q, and_3_out, Q_bar);
  nor nor_4 (Q_bar, Q, and_4_out);
endmodule
