// Logisim project FullAdder2.circ as structural Verilog: 1 circuit, main circuit main
// Full Adder
module main (
  input  Carry_in,
  input  A_in,
  input  B_in,
  output Sum,
  output Carry
);

  wire main_1_carry, main_2_carry, main_2_sum;

  HalfAdder_main main_1 (.A_in(Carry_in), .B_in(main_2_sum), .Sum(Sum), .Carry(main_1_carry));
  HalfAdder_main main_2 (.A_in(A_in), .B_in(B_in), .Sum(main_2_sum), .Carry(main_2_carry));
  or or_1 (Carry, main_1_carry, main_2_carry);
endmodule
