// Logisim project HalfAdder.circ as structural Verilog: 1 circuit, main circuit main
// Half Adder
module main (
  input  A_in,
  input  B_in,
  output Sum,
  output Carry
);

  xor xor_1 (Sum, A_in, B_in);
  and and_1 (Carry, A_in, B_in);
endmodule
