// Logisim project Selector.circ as structural Verilog: 1 circuit, main circuit main
// Select
module main (
  input  B,
  input  Sel,
  input  A,
  output Out
);

  wire and_1_out, and_2_out, not_1_out;

  not not_1 (not_1_out, Sel);
  and and_1 (and_1_out, B, Sel);
  and and_2 (and_2_out, A, not_1_out);
  or or_1 (Out, and_1_out, and_2_out);
endmodule
