// Logisim project 4 bit clear D type latch.circ as structural Verilog: 1 circuit, main circuit main
// 4bit latch
module main (
  input  Clear,
  input  D3,
  input  D2,
  input  D1,
  input  D0,
  input  Clk,
  output Q3,
  output Q2,
  output Q1,
  output Q0
);

  Clear_D_type_latch_main main_1 (.Clear(Clear), .Clock(Clk), .Data(D3), .Q(Q3));
  Clear_D_type_latch_main main_2 (.Clear(Clear), .Clock(Clk), .Data(D2), .Q(Q2));
  Clear_D_type_latch_main main_3 (.Clear(Clear), .Clock(Clk), .Data(D1), .Q(Q1));
  Clear_D_type_latch_main main_4 (.Clear(Clear), .Clock(Clk), .Data(D0), .Q(Q0));
endmodule
