// Logisim project 8 bit adder with ones complement page 150.circ as structural Verilog: 1 circuit, main circuit main
module main (
  input  B7,
  input  B6,
  input  B5,
  input  B4,
  input  B3,
  input  B2,
  input  B1,
  input  B0,
  input  in_9,
  input  Invert,
  input  A7,
  input  A6,
  input  A5,
  input  A4,
  input  A3,
  input  A2,
  input  A1,
  input  A0,
  input  CI,
  input  in_20,
  input  Overflow,
  output out_22,
  output out_23,
  output out_24,
  output out_25,
  output out_26,
  output out_27,
  output out_28,
  output out_29
);

  wire main_1_out_10, main_1_out_11, main_1_out_12, main_1_out_13, main_1_out_14, main_1_out_15,
       main_1_out_16, main_1_out_17, main_2_co;

  xor xor_1 (Overflow, main_2_co, CI);
  Invert_main main_1 (
    .Invert(CI), .in_1(B7), .in_2(B6), .in_3(B5), .in_4(B4), .in_5(B3), .in_6(B2), .in_7(B1), .in_8(B0),
    .out_10(main_1_out_10), .out_11(main_1_out_11), .out_12(main_1_out_12), .out_13(main_1_out_13),
    .out_14(main_1_out_14), .out_15(main_1_out_15), .out_16(main_1_out_16), .out_17(main_1_out_17));
  _8BitAdder_main main_2 (
    .CO(main_2_co), .A7(A7), .A6(A6), .A5(A5), .A4(A4), .A3(A3), .A2(A2), .A1(A1), .A0(A0),
    .B7(main_1_out_10), .B6(main_1_out_11), .B5(main_1_out_12), .B4(main_1_out_13), .B3(main_1_out_14),
    .B2(main_1_out_15), .B1(main_1_out_16), .B0(main_1_out_17), .S7(out_22), .S6(out_23), .S5(out_24),
    .S4(out_25), .S3(out_26), .S2(out_27), .S1(out_28), .S0(out_29), .CI(CI));

  assign in_9 = CI;
  assign in_20 = CI;
  assign Invert = CI;
endmodule
