// Logisim project 8 bit count with Ocelator.circ as structural Verilog: 1 circuit, main circuit main
module main (
  input  in_1,
  output out_2,
  output out_3,
  output out_4,
  output out_5,
  output out_6,
  output out_7,
  output out_8,
  output out_9
);

  wire main_1_clk_bar;

  not not_1 (in_1, in_1);
  _8_bit_ripple_counter_main main_1 (
    .Clk(in_1), .Clk_bar(main_1_clk_bar), .Q7(out_2), .Q6(out_3), .Q5(out_4), .Q4(out_5), .Q3(out_6),
    .Q2(out_7), .Q1(out_8), .Q0(out_9));
  // also tied to GND on the sheet: main_1_clk_bar
endmodule
