// Logisim project Counter page 170.circ as structural Verilog: 1 circuit, main circuit main
// Counter
module main (
  input  S7,
  input  S6,
  input  S5,
  input  S4,
  input  S3,
  input  S2,
  input  S1,
  input  S0,
  input  Clear,
  input  Add,
  output Out7,
  output Out6,
  output Out5,
  output Out4,
  output Out3,
  output Out2,
  output Out1,
  output Out0
);

  wire main_2_s0, main_2_s1, main_2_s2, main_2_s3, main_2_s4, main_2_s5, main_2_s6, main_2_s7;

  _8_bit_clear_D_type_latch_main main_1 (
    .Clk(Add), .Clear(Clear), .D7(main_2_s7), .D6(main_2_s6), .D5(main_2_s5), .D4(main_2_s4), .D3(main_2_s3),
    .D2(main_2_s2), .D1(main_2_s1), .D0(main_2_s0), .Q7(Out7), .Q6(Out6), .Q5(Out5), .Q4(Out4), .Q3(Out3),
    .Q2(Out2), .Q1(Out1), .Q0(Out0));
  _8BitAdder_main main_2 (
    .A7(S7), .A6(S6), .A5(S5), .A4(S4), .A3(S3), .A2(S2), .A1(S1), .A0(S0), .B7(Out7), .B6(Out6), .B5(Out5),
    .B4(Out4), .B3(Out3), .B2(Out2), .B1(Out1), .B0(Out0), .S7(main_2_s7), .S6(main_2_s6), .S5(main_2_s5),
    .S4(main_2_s4), .S3(main_2_s3), .S2(main_2_s2), .S1(main_2_s1), .S0(main_2_s0), .CI(1'b0));  // open: CO
endmodule
