// Logisim project Counter2.circ as structural Verilog: 1 circuit, main circuit main
module main (
  input  in_1,
  input  in_2,
  input  in_3,
  input  in_4,
  input  in_5,
  input  in_6,
  input  in_7,
  input  in_8,
  input  in_9,
  input  in_10
);

  wire main_1_out0, main_1_out1, main_1_out2, main_1_out3, main_1_out4, main_1_out5, main_1_out6, main_1_out7;

  LED led_1 (.in(main_1_out7));
  LED led_2 (.in(main_1_out4));
  LED led_3 (.in(main_1_out5));
  LED led_4 (.in(main_1_out6));
  Counter_main main_1 (
    .Clear(in_9), .S7(in_1), .S6(in_2), .S5(in_3), .S4(in_4), .S3(in_5), .S2(in_6), .S1(in_7), .S0(in_8),
    .Out7(main_1_out7), .Out6(main_1_out6), .Out5(main_1_out5), .Out4(main_1_out4), .Out3(main_1_out3),
    .Out2(main_1_out2), .Out1(main_1_out1), .Out0(main_1_out0), .Add(in_10));
  LED led_5 (.in(main_1_out2));
  LED led_6 (.in(main_1_out3));
  LED led_7 (.in(main_1_out0));
  LED led_8 (.in(main_1_out1));
endmodule
