// Logisim project DMux4Way.circ as structural Verilog: 1 circuit, main circuit main
module main (
  input  in,
  input  sel0,
  input  sel1,
  output a,
  output b,
  output c,
  output d
);

  wire main_2_a, main_2_b;

  DMux_main main_1 (.in(main_2_b), .sel(sel1), .a(c), .b(d));
  DMux_main main_2 (.in(in), .sel(sel0), .a(main_2_a), .b(main_2_b));
  DMux_main main_3 (.in(main_2_a), .sel(sel1), .a(a), .b(b));
endmodule
