// Logisim project DMux8Way.circ as structural Verilog: 1 circuit, main circuit main
module main (
  input  in,
  input  sel0,
  input  sel1,
  input  sel2,
  output a,
  output b,
  output c,
  output d,
  output e,
  output f,
  output g,
  output h
);

  wire main_2_a, main_2_b;

  DMux4Way_main main_1 (.sel0(sel1), .sel1(sel2), .in(main_2_a), .a(a), .b(b), .c(c), .d(d));
  DMux_main main_2 (.in(in), .sel(sel0), .a(main_2_a), .b(main_2_b));
  DMux4Way_main main_3 (.sel0(sel1), .sel1(sel2), .in(main_2_b), .a(e), .b(f), .c(g), .d(h));
endmodule
