// Logisim project Invert.circ as structural Verilog: 1 circuit, main circuit main
// Invert
module main (
  input  in_1,
  input  in_2,
  input  in_3,
  input  in_4,
  input  in_5,
  input  in_6,
  input  in_7,
  input  in_8,
  input  Invert,
  output out_10,
  output out_11,
  output out_12,
  output out_13,
  output out_14,
  output out_15,
  output out_16,
  output out_17
);

  xor xor_1 (out_10, Invert, in_1);
  xor xor_2 (out_11, Invert, in_2);
  xor xor_3 (out_12, Invert, in_3);
  xor xor_4 (out_13, Invert, in_4);
  xor xor_5 (out_15, Invert, in_6);
  xor xor_6 (out_14, Invert, in_5);
  xor xor_7 (out_16, Invert, in_7);
  xor xor_8 (out_17, Invert, in_8);
endmodule
