// Logisim project Mux16.circ as structural Verilog: 1 circuit, main circuit main
module main (
  input  in_1,
  input  in_2,
  input  in_3,
  input  in_4,
  input  in_5,
  input  in_6,
  input  in_7,
  input  in_8,
  input  in_9,
  input  in_10,
  input  in_11,
  input  in_12,
  input  in_13,
  input  in_14,
  input  in_15,
  input  in_16,
  input  in_17,
  input  in_18,
  input  in_19,
  input  in_20,
  input  in_21,
  input  in_22,
  input  in_23,
  input  in_24,
  input  in_25,
  input  in_26,
  input  in_27,
  input  in_28,
  input  in_29,
  input  in_30,
  input  in_31,
  input  in_32,
  input  sel,
  output out_34,
  output out_35,
  output out_36,
  output out_37,
  output out_38,
  output out_39,
  output out_40,
  output out_41,
  output out_42,
  output out_43,
  output out_44,
  output out_45,
  output out_46,
  output out_47,
  output out_48,
  output out_49
);

  mux_main main_1 (.a(in_1), .Sel(sel), .b(in_17), .out(out_34));
  mux_main main_2 (.a(in_2), .Sel(sel), .b(in_18), .out(out_35));
  mux_main main_3 (.a(in_3), .Sel(sel), .b(in_19), .out(out_36));
  mux_main main_4 (.a(in_4), .Sel(sel), .b(in_20), .out(out_37));
  mux_main main_5 (.a(in_6), .Sel(sel), .b(in_22), .out(out_39));
  mux_main main_6 (.a(in_5), .Sel(sel), .b(in_21), .out(out_38));
  mux_main main_7 (.a(in_7), .Sel(sel), .b(in_23), .out(out_40));
  mux_main main_8 (.a(in_8), .Sel(sel), .b(in_24), .out(out_41));
  mux_main main_9 (.a(in_9), .Sel(sel), .b(in_25), .out(out_42));
  mux_main main_10 (.a(in_10), .Sel(sel), .b(in_26), .out(out_43));
  mux_main main_11 (.a(in_12), .Sel(sel), .b(in_28), .out(out_45));
  mux_main main_12 (.a(in_11), .Sel(sel), .b(in_27), .out(out_44));
  mux_main main_13 (.a(in_14), .Sel(sel), .b(in_30), .out(out_47));
  mux_main main_14 (.a(in_13), .Sel(sel), .b(in_29), .out(out_46));
  mux_main main_15 (.a(in_15), .Sel(sel), .b(in_31), .out(out_48));
  mux_main main_16 (.a(in_16), .Sel(sel), .b(in_32), .out(out_49));
endmodule
