// Logisim project Mux4Way16.circ as structural Verilog: 1 circuit, main circuit main
module main (
  input  A15,
  input  A14,
  input  A13,
  input  A12,
  input  A11,
  input  A10,
  input  A9,
  input  A8,
  input  A7,
  input  A6,
  input  A5,
  input  A4,
  input  A3,
  input  A2,
  input  A1,
  input  A0,
  input  in_17,
  input  in_18,
  input  in_19,
  input  in_20,
  input  in_21,
  input  in_22,
  input  in_23,
  input  in_24,
  input  in_25,
  input  in_26,
  input  in_27,
  input  in_28,
  input  in_29,
  input  in_30,
  input  in_31,
  input  in_32,
  input  in_33,
  input  in_34,
  input  in_35,
  input  in_36,
  input  in_37,
  input  in_38,
  input  in_39,
  input  in_40,
  input  in_41,
  input  in_42,
  input  in_43,
  input  in_44,
  input  in_45,
  input  in_46,
  input  in_47,
  input  in_48,
  input  in_49,
  input  in_50,
  input  in_51,
  input  in_52,
  input  in_53,
  input  in_54,
  input  in_55,
  input  in_56,
  input  in_57,
  input  in_58,
  input  in_59,
  input  in_60,
  input  in_61,
  input  in_62,
  input  in_63,
  input  in_64,
  input  sel0,
  input  sel1,
  output out_67,
  output out_68,
  output out_69,
  output out_70,
  output out_71,
  output out_72,
  output out_73,
  output out_74,
  output out_75,
  output out_76,
  output out_77,
  output out_78,
  output out_79,
  output out_80,
  output out_81,
  output out_82
);

  wire [15:0] main_1_out_49, main_3_out_49;

  Mux16_main main_1 (
    .sel(sel0), .in_1(A15), .in_2(A14), .in_3(A13), .in_4(A12), .in_5(A11), .in_6(A10), .in_7(A9), .in_8(A8),
    .in_9(A7), .in_10(A6), .in_11(A5), .in_12(A4), .in_13(A3), .in_14(A2), .in_15(A1), .in_16(A0),
    .in_17(in_33), .in_18(in_34), .in_19(in_35), .in_20(in_36), .in_21(in_37), .in_22(in_38), .in_23(in_39),
    .in_24(in_40), .in_25(in_41), .in_26(in_42), .in_27(in_43), .in_28(in_44), .in_29(in_45), .in_30(in_46),
    .in_31(in_47), .in_32(in_48), .out_34(main_1_out_49[15]), .out_35(main_1_out_49[14]),
    .out_36(main_1_out_49[13]), .out_37(main_1_out_49[12]), .out_38(main_1_out_49[11]),
    .out_39(main_1_out_49[10]), .out_40(main_1_out_49[9]), .out_41(main_1_out_49[8]),
    .out_42(main_1_out_49[7]), .out_43(main_1_out_49[6]), .out_44(main_1_out_49[5]),
    .out_45(main_1_out_49[4]), .out_46(main_1_out_49[3]), .out_47(main_1_out_49[2]),
    .out_48(main_1_out_49[1]), .out_49(main_1_out_49[0]));
  Mux16_main main_2 (
    .sel(sel1), .in_1(main_1_out_49[15]), .in_2(main_1_out_49[14]), .in_3(main_1_out_49[13]),
    .in_4(main_1_out_49[12]), .in_5(main_1_out_49[11]), .in_6(main_1_out_49[10]), .in_7(main_1_out_49[9]),
    .in_8(main_1_out_49[8]), .in_9(main_1_out_49[7]), .in_10(main_1_out_49[6]), .in_11(main_1_out_49[5]),
    .in_12(main_1_out_49[4]), .in_13(main_1_out_49[3]), .in_14(main_1_out_49[2]), .in_15(main_1_out_49[1]),
    .in_16(main_1_out_49[0]), .in_17(main_3_out_49[15]), .in_18(main_3_out_49[14]),
    .in_19(main_3_out_49[13]), .in_20(main_3_out_49[12]), .in_21(main_3_out_49[11]),
    .in_22(main_3_out_49[10]), .in_23(main_3_out_49[9]), .in_24(main_3_out_49[8]), .in_25(main_3_out_49[7]),
    .in_26(main_3_out_49[6]), .in_27(main_3_out_49[5]), .in_28(main_3_out_49[4]), .in_29(main_3_out_49[3]),
    .in_30(main_3_out_49[2]), .in_31(main_3_out_49[1]), .in_32(main_3_out_49[0]), .out_34(out_67),
    .out_35(out_68), .out_36(out_69), .out_37(out_70), .out_38(out_71), .out_39(out_72), .out_40(out_73),
    .out_41(out_74), .out_42(out_75), .out_43(out_76), .out_44(out_77), .out_45(out_78), .out_46(out_79),
    .out_47(out_80), .out_48(out_81), .out_49(out_82));
  Mux16_main main_3 (
    .sel(sel0), .in_1(in_17), .in_2(in_18), .in_3(in_19), .in_4(in_20), .in_5(in_21), .in_6(in_22),
    .in_7(in_23), .in_8(in_24), .in_9(in_25), .in_10(in_26), .in_11(in_27), .in_12(in_28), .in_13(in_29),
    .in_14(in_30), .in_15(in_31), .in_16(in_32), .in_17(in_49), .in_18(in_50), .in_19(in_51), .in_20(in_52),
    .in_21(in_53), .in_22(in_54), .in_23(in_55), .in_24(in_56), .in_25(in_57), .in_26(in_58), .in_27(in_59),
    .in_28(in_60), .in_29(in_61), .in_30(in_62), .in_31(in_63), .in_32(in_64), .out_34(main_3_out_49[15]),
    .out_35(main_3_out_49[14]), .out_36(main_3_out_49[13]), .out_37(main_3_out_49[12]),
    .out_38(main_3_out_49[11]), .out_39(main_3_out_49[10]), .out_40(main_3_out_49[9]),
    .out_41(main_3_out_49[8]), .out_42(main_3_out_49[7]), .out_43(main_3_out_49[6]),
    .out_44(main_3_out_49[5]), .out_45(main_3_out_49[4]), .out_46(main_3_out_49[3]),
    .out_47(main_3_out_49[2]), .out_48(main_3_out_49[1]), .out_49(main_3_out_49[0]));
endmodule
