// Logisim project Ripple Counter sub circuit model.circ as structural Verilog: 1 circuit, main circuit main
module main (
  input  in_1,
  output out_2,
  output out_3,
  output out_4,
  output out_5,
  output out_6,
  output out_7,
  output out_8,
  output out_9
);

  Ripple_Counter_sub_circuit_main main_1 (
    .Clk(in_1), .out7(out_2), .out6(out_6), .out5(out_3), .out4(out_7), .out3(out_4), .out2(out_8),
    .out1(out_5), .out0(out_9));
endmodule
