// Logisim project level triggered D type latch.circ as structural Verilog: 1 circuit, main circuit main
// L D-type Latch
module main (
  input  Clock,
  input  Data,
  output Q
);

  wire and_1_out, and_2_out, nor_2_out, not_1_out;

  not not_1 (not_1_out, Data);
  and and_1 (and_1_out, not_1_out, Clock);
  and and_2 (and_2_out, Clock, Data);
  nor nor_1 (Q, and_1_out, nor_2_out);
  nor nor_2 (nor_2_out, Q, and_2_out);
endmodule
