// Logisim project 4 bit Add-Sub.circ as structural Verilog: 1 circuit, main circuit main
module main (
  input  _1s,
  input  in_2,
  input  _2s,
  input  in_4,
  input  _4s,
  input  in_6,
  input  _8s,
  input  in_8,
  input  V
);

  wire and_1_out, and_2_out, and_3_out, and_4_out, and_5_out, and_6_out, and_7_out, and_8_out, not_1_out,
       or_1_out, or_2_out, or_3_out, or_4_out, xor_1_out, xor_2_out, xor_3_out, xor_4_out, xor_5_out,
       xor_6_out, xor_7_out, xor_8_out, xor_9_out, xor_10_out, xor_11_out, xor_12_out, xor_13_out;

  not not_1 (not_1_out, V);
  xor xor_1 (xor_1_out, in_2, not_1_out);
  xor xor_2 (xor_2_out, in_4, not_1_out);
  xor xor_3 (xor_3_out, in_6, not_1_out);
  xor xor_4 (xor_4_out, in_8, not_1_out);
  xor xor_5 (xor_5_out, _1s, xor_1_out);
  and and_1 (and_1_out, _1s, xor_1_out);
  xor xor_6 (xor_6_out, _4s, xor_3_out);
  and and_2 (and_2_out, _4s, xor_3_out);
  xor xor_7 (xor_7_out, not_1_out, xor_5_out);
  and and_3 (and_3_out, not_1_out, xor_5_out);
  xor xor_8 (xor_8_out, or_3_out, xor_6_out);
  and and_4 (and_4_out, or_3_out, xor_6_out);
  or or_1 (or_1_out, and_3_out, and_1_out);
  or or_2 (or_2_out, and_4_out, and_2_out);
  xor xor_9 (xor_9_out, _2s, xor_2_out);
  and and_5 (and_5_out, _2s, xor_2_out);
  xor xor_10 (xor_10_out, _8s, xor_4_out);
  and and_6 (and_6_out, _8s, xor_4_out);
  xor xor_11 (xor_11_out, or_1_out, xor_9_out);
  and and_7 (and_7_out, or_1_out, xor_9_out);
  xor xor_12 (xor_12_out, or_2_out, xor_10_out);
  and and_8 (and_8_out, or_2_out, xor_10_out);
  or or_3 (or_3_out, and_7_out, and_5_out);
  or or_4 (or_4_out, and_8_out, and_6_out);
  xor xor_13 (xor_13_out, or_4_out, not_1_out);
  LED led_1 (.in(xor_7_out));
  LED led_2 (.in(xor_11_out));
  LED led_3 (.in(xor_8_out));
  LED led_4 (.in(xor_12_out));
  LED led_5 (.in(xor_13_out));

  // Notes on the sheet:
  //   A Input
  //   V
  //   B Input
  //   V
  //   1 for addition - 0 for subtraction
  //   4 Bit Adder modified for subtraction as well
  //   1s
  //   2s
  //   4s
  //   8s
  //   ^
  //   Overflow / Underflow
endmodule
