// Logisim project 4 bit level triggered D type latch 2 output.circ as structural Verilog: 1 circuit, main circuit main
// 4 bit latch out 2
module main (
  input  D3,
  input  D2,
  input  D1,
  input  D0,
  input  Clk,
  input  Q3,
  input  Q2,
  input  Q1,
  input  Q0,
  input  Q3_2,
  input  Q2_2,
  input  Q1_2,
  input  Q0_2
);

  level_triggered_D_type_flip_flop_main main_1 (.Clock(Clk), .Data(D3), .Q(Q3), .Q_bar(Q3_2));
  level_triggered_D_type_flip_flop_main main_2 (.Clock(Clk), .Data(D2), .Q(Q2), .Q_bar(Q2_2));
  level_triggered_D_type_flip_flop_main main_3 (.Clock(Clk), .Data(D1), .Q(Q1), .Q_bar(Q1_2));
  level_triggered_D_type_flip_flop_main main_4 (.Clock(Clk), .Data(D0), .Q(Q0), .Q_bar(Q0_2));
endmodule
