// Logisim project 4BitAdder.circ as structural Verilog: 1 circuit, main circuit main
module main (
  input  A3,
  input  A2,
  input  A1,
  input  A0,
  input  B3,
  input  B2,
  input  B1,
  input  B0,
  input  CI,
  output Overflow,
  output Sum4,
  output Sum3,
  output Sum2,
  output Sum1
);

  wire main_2_carry, main_3_carry, main_4_carry;

  FullAdder2_main main_1 (.Carry_in(main_2_carry), .A_in(A3), .B_in(B3), .Sum(Sum4), .Carry(Overflow));
  FullAdder2_main main_2 (.Carry_in(main_3_carry), .A_in(A2), .B_in(B2), .Sum(Sum3), .Carry(main_2_carry));
  FullAdder2_main main_3 (.Carry_in(main_4_carry), .A_in(A1), .B_in(B1), .Sum(Sum2), .Carry(main_3_carry));
  FullAdder2_main main_4 (.Carry_in(CI), .A_in(A0), .B_in(B0), .Sum(Sum1), .Carry(main_4_carry));
endmodule
