// Logisim project 4BitAdderSub.circ as structural Verilog: 1 circuit, main circuit main
module main (
  input  Add_Sub,
  input  A3,
  input  A2,
  input  A1,
  input  A0,
  input  B3,
  input  B2,
  input  B1,
  input  B0,
  output Overflow,
  output Sum4,
  output Sum3,
  output Sum2,
  output Sum1
);

  wire main_1_carry, main_2_carry, main_3_carry, main_4_carry, xor_2_out, xor_3_out, xor_4_out, xor_5_out;

  xor xor_1 (Overflow, Add_Sub, main_1_carry);
  xor xor_2 (xor_2_out, Add_Sub, B3);
  FullAdder2_main main_1 (.Carry_in(main_2_carry), .A_in(A3), .B_in(xor_2_out), .Sum(Sum4), .Carry(main_1_carry));
  xor xor_3 (xor_3_out, Add_Sub, B2);
  xor xor_4 (xor_4_out, Add_Sub, B1);
  FullAdder2_main main_2 (.Carry_in(main_3_carry), .A_in(A2), .B_in(xor_3_out), .Sum(Sum3), .Carry(main_2_carry));
  xor xor_5 (xor_5_out, Add_Sub, B0);
  FullAdder2_main main_3 (.Carry_in(main_4_carry), .A_in(A1), .B_in(xor_4_out), .Sum(Sum2), .Carry(main_3_carry));
  FullAdder2_main main_4 (.Carry_in(Add_Sub), .A_in(A0), .B_in(xor_5_out), .Sum(Sum1), .Carry(main_4_carry));
endmodule
