// Logisim project 8 bit ripple counter - from system.circ as structural Verilog: 1 circuit, main circuit main
module main (
  output out_1,
  output out_2,
  output out_3,
  output out_4,
  output out_5,
  output out_6,
  output out_7,
  output out_8
);

  wire d_ff_1_qn, d_ff_2_qn, d_ff_3_qn, d_ff_4_qn, undriven;

  D_Flip_Flop d_ff_1 (.clk(undriven), .D(d_ff_1_qn), .Q(out_1), .Qn(d_ff_1_qn));  // open: preset, en, reset
  D_Flip_Flop d_ff_2 (.D(d_ff_2_qn), .Q(out_2), .Qn(d_ff_2_qn));  // open: clk, preset, en, reset
  D_Flip_Flop d_ff_3 (.D(d_ff_3_qn), .Q(out_3), .Qn(d_ff_3_qn));  // open: clk, preset, en, reset
  D_Flip_Flop d_ff_4 (.D(d_ff_4_qn), .Q(out_4), .Qn(d_ff_4_qn));  // open: clk, preset, en, reset
  D_Flip_Flop d_ff_5 (.Q(out_5));  // open: clk, D, Qn, preset, en, reset
  D_Flip_Flop d_ff_6 (.Q(out_6));  // open: clk, D, Qn, preset, en, reset
  D_Flip_Flop d_ff_7 (.Q(out_7));  // open: clk, D, Qn, preset, en, reset
  D_Flip_Flop d_ff_8 (.Q(out_8));  // open: clk, D, Qn, preset, en, reset
endmodule
