// Logisim project 8 bit ripple counter.circ as structural Verilog: 1 circuit, main circuit main
// 8 bit count
module main (
  input  Clk,
  output Clk_bar,
  output Q7,
  output Q6,
  output Q5,
  output Q4,
  output Q3,
  output Q2,
  output Q1,
  output Q0
);

  wire main_1_q_bar, main_2_q_bar, main_3_q_bar, main_4_q_bar, main_5_q_bar, main_6_q_bar, main_7_q_bar,
       main_8_q_bar;

  not not_1 (Clk_bar, Clk);
  Edgel_triggered_D_type_latch_main main_1 (.Data(main_1_q_bar), .Clk(Clk), .Q(Q7), .Q_bar(main_1_q_bar));
  Edgel_triggered_D_type_latch_main main_2 (.Data(main_2_q_bar), .Clk(main_1_q_bar), .Q(Q6), .Q_bar(main_2_q_bar));
  Edgel_triggered_D_type_latch_main main_3 (.Data(main_3_q_bar), .Clk(main_2_q_bar), .Q(Q5), .Q_bar(main_3_q_bar));
  Edgel_triggered_D_type_latch_main main_4 (.Data(main_4_q_bar), .Clk(main_3_q_bar), .Q(Q4), .Q_bar(main_4_q_bar));
  Edgel_triggered_D_type_latch_main main_5 (.Data(main_5_q_bar), .Clk(main_4_q_bar), .Q(Q3), .Q_bar(main_5_q_bar));
  Edgel_triggered_D_type_latch_main main_6 (.Data(main_6_q_bar), .Clk(main_5_q_bar), .Q(Q2), .Q_bar(main_6_q_bar));
  Edgel_triggered_D_type_latch_main main_7 (.Data(main_7_q_bar), .Clk(main_6_q_bar), .Q(Q1), .Q_bar(main_7_q_bar));
  Edgel_triggered_D_type_latch_main main_8 (.Data(main_8_q_bar), .Clk(main_7_q_bar), .Q(Q0), .Q_bar(main_8_q_bar));
endmodule
