// Logisim project Clear D type latch.circ as structural Verilog: 1 circuit, main circuit main
// L D-type Latch
module main (
  input  Clear,
  input  Clock,
  input  Data,
  output Q
);

  wire and_1_out, and_2_out, nor_2_out, not_1_out, or_1_out;

  not not_1 (not_1_out, Data);
  and and_1 (and_1_out, not_1_out, Clock);
  and and_2 (and_2_out, Clock, Data);
  or or_1 (or_1_out, Clear, and_1_out);
  nor nor_1 (Q, or_1_out, nor_2_out);
  nor nor_2 (nor_2_out, Q, and_2_out);
endmodule
