// Logisim project EQ3.circ as structural Verilog: 1 circuit, main circuit main
// EQ3
module main (
  input  in_1,
  input  in_2,
  input  in_3,
  input  in_4,
  input  in_5,
  input  in_6,
  output out_7
);

  wire or_1_out, or_2_out, xor_1_out, xor_2_out, xor_3_out;

  xor xor_1 (xor_1_out, in_1, in_4);
  xor xor_2 (xor_2_out, in_2, in_5);
  xor xor_3 (xor_3_out, in_3, in_6);
  or or_1 (or_1_out, xor_1_out, xor_2_out);
  or or_2 (or_2_out, or_1_out, xor_3_out);
  not not_1 (out_7, or_2_out);
endmodule
