// Logisim project Edge triggered D type latch with preset and clear.circ as structural Verilog: 1 circuit, main circuit main
// Edge Latch
module main (
  input  Preset,
  input  Clock,
  input  Data,
  input  Clear,
  output Q,
  output Q_bar
);

  wire nor_1_out, nor_2_out, nor_3_out, nor_4_out, not_1_out;

  not not_1 (not_1_out, Clock);
  nor nor_1 (nor_1_out, Clear, nor_4_out, nor_2_out);
  nor nor_2 (nor_2_out, nor_1_out, Preset, not_1_out);
  nor nor_3 (nor_3_out, nor_2_out, not_1_out, nor_4_out);
  nor nor_4 (nor_4_out, nor_3_out, Preset, Data);
  nor nor_5 (Q, Clear, nor_2_out, Q_bar);
  nor nor_6 (Q_bar, Q, Preset, nor_3_out);
endmodule
