// Logisim project R-S Flip Flop.circ as structural Verilog: 1 circuit, main circuit main
// RS Flip Flop
module main (
  input  R,
  input  S,
  output Q,
  output Q_bar
);

  nor nor_1 (Q, R, Q_bar);
  nor nor_2 (Q_bar, Q, S);
endmodule
