// Logisim project Save.circ as structural Verilog: 1 circuit, main circuit main
// Save
module main (
  input  _2S7,
  input  _2S6,
  input  _2S5,
  input  _2S4,
  input  _2S3,
  input  _2S2,
  input  _2S1,
  input  _2S0,
  input  Save,
  input  _1S7,
  input  _1S6,
  input  _1S5,
  input  _1S4,
  input  _1S3,
  input  _1S2,
  input  _1S1,
  input  _1S0,
  input  Sel,
  input  CI,
  output Out,
  output Out7,
  output Out6,
  output Out5,
  output Out4,
  output Out3,
  output Out2,
  output Out1,
  output Out0
);

  wire main_1_out0, main_1_out1, main_1_out2, main_1_out3, main_1_out4, main_1_out5, main_1_out6,
       main_1_out7, main_3_q0, main_3_q1, main_3_q2, main_3_q3, main_3_q4, main_3_q5, main_3_q6, main_3_q7;

  _8bit_Selector_main main_1 (
    .Sel(Sel), .A7(_1S7), .A6(_1S6), .A5(_1S5), .A4(_1S4), .A3(_1S3), .A2(_1S2), .A1(_1S1), .A0(_1S0),
    .B7(main_3_q7), .B6(main_3_q6), .B5(main_3_q5), .B4(main_3_q4), .B3(main_3_q3), .B2(main_3_q2),
    .B1(main_3_q1), .B0(main_3_q0), .Out7(main_1_out7), .Out6(main_1_out6), .Out5(main_1_out5),
    .Out4(main_1_out4), .Out3(main_1_out3), .Out2(main_1_out2), .Out1(main_1_out1), .Out0(main_1_out0));
  _8BitAdder_main main_2 (
    .CO(Out), .A7(_2S7), .A6(_2S6), .A5(_2S5), .A4(_2S4), .A3(_2S3), .A2(_2S2), .A1(_2S1), .A0(_2S0),
    .B7(main_1_out7), .B6(main_1_out6), .B5(main_1_out5), .B4(main_1_out4), .B3(main_1_out3),
    .B2(main_1_out2), .B1(main_1_out1), .B0(main_1_out0), .S7(Out7), .S6(Out6), .S5(Out5), .S4(Out4),
    .S3(Out3), .S2(Out2), .S1(Out1), .S0(Out0), .CI(CI));
  _8_bit_level_triggered_D_type_latch_main main_3 (
    .Clk(Save), .D7(Out7), .D6(Out6), .D5(Out5), .D4(Out4), .D3(Out3), .D2(Out2), .D1(Out1), .D0(Out0),
    .Q7(main_3_q7), .Q6(main_3_q6), .Q5(main_3_q5), .Q4(main_3_q4), .Q3(main_3_q3), .Q2(main_3_q2),
    .Q1(main_3_q1), .Q0(main_3_q0));
endmodule
