// Logisim project mux.circ as structural Verilog: 1 circuit, main circuit main
module main (
  input  a,
  input  Sel,
  input  b,
  output out
);

  wire nand_1_out, nand_2_out, not_1_out, not_2_out;

  not not_1 (not_1_out, Sel);
  not not_2 (not_2_out, not_1_out);
  nand nand_1 (nand_1_out, a, not_1_out);
  nand nand_2 (nand_2_out, not_2_out, b);
  nand nand_3 (out, nand_1_out, nand_2_out);

  // Notes on the sheet:
  //   a
  //   sel
  //   nsel
  //   b
  //   nout1
  //   nout2
  //   out
endmodule
