// Logisim project 4 bit level triggered D type latch.circ as structural Verilog: 1 circuit, main circuit main
// 4bit latch
module main (
  input  D3,
  input  D2,
  input  D1,
  input  D0,
  input  Clk,
  output Q3,
  output Q2,
  output Q1,
  output Q0
);

  level_triggered_D_type_latch_main main_1 (.Clock(Clk), .Data(D3), .Q(Q3));
  level_triggered_D_type_latch_main main_2 (.Clock(Clk), .Data(D2), .Q(Q2));
  level_triggered_D_type_latch_main main_3 (.Clock(Clk), .Data(D1), .Q(Q1));
  level_triggered_D_type_latch_main main_4 (.Clock(Clk), .Data(D0), .Q(Q0));
endmodule
