// Logisim project 8 Bit Add and Subtract.circ as structural Verilog: 1 circuit, main circuit main
module main (
  input  Add_Sub,
  input  A7,
  input  A6,
  input  A5,
  input  A4,
  input  A3,
  input  A2,
  input  A1,
  input  A0,
  input  B7,
  input  B6,
  input  B5,
  input  B4,
  input  B3,
  input  B2,
  input  B1,
  input  B0,
  output Overflow,
  output Sum7,
  output Sum6,
  output Sum5,
  output Sum4,
  output Sum3,
  output Sum2,
  output Sum1,
  output Sum0
);

  wire main_1_carry, main_2_carry, main_3_carry, main_4_carry, main_5_carry, main_6_carry, main_7_carry,
       main_8_carry, xor_2_out, xor_3_out, xor_4_out, xor_5_out, xor_6_out, xor_7_out, xor_8_out, xor_9_out;

  xor xor_1 (Overflow, Add_Sub, main_1_carry);
  xor xor_2 (xor_2_out, Add_Sub, B7);
  xor xor_3 (xor_3_out, Add_Sub, B6);
  FullAdder2_main main_1 (.Carry_in(main_2_carry), .A_in(A7), .B_in(xor_2_out), .Sum(Sum7), .Carry(main_1_carry));
  xor xor_4 (xor_4_out, Add_Sub, B5);
  FullAdder2_main main_2 (.Carry_in(main_4_carry), .A_in(A6), .B_in(xor_3_out), .Sum(Sum6), .Carry(main_2_carry));
  xor xor_5 (xor_5_out, Add_Sub, B4);
  FullAdder2_main main_3 (.Carry_in(main_5_carry), .A_in(A4), .B_in(xor_5_out), .Sum(Sum4), .Carry(main_3_carry));
  FullAdder2_main main_4 (.Carry_in(main_3_carry), .A_in(A5), .B_in(xor_4_out), .Sum(Sum5), .Carry(main_4_carry));
  xor xor_6 (xor_6_out, Add_Sub, B3);
  xor xor_7 (xor_7_out, Add_Sub, B2);
  FullAdder2_main main_5 (.Carry_in(main_6_carry), .A_in(A3), .B_in(xor_6_out), .Sum(Sum3), .Carry(main_5_carry));
  xor xor_8 (xor_8_out, Add_Sub, B1);
  FullAdder2_main main_6 (.Carry_in(main_8_carry), .A_in(A2), .B_in(xor_7_out), .Sum(Sum2), .Carry(main_6_carry));
  xor xor_9 (xor_9_out, Add_Sub, B0);
  FullAdder2_main main_7 (.Carry_in(Add_Sub), .A_in(A0), .B_in(xor_9_out), .Sum(Sum0), .Carry(main_7_carry));
  FullAdder2_main main_8 (.Carry_in(main_7_carry), .A_in(A1), .B_in(xor_8_out), .Sum(Sum1), .Carry(main_8_carry));

  // Notes on the sheet:
  //   8 Bit Addition and Subtraction Circuit
endmodule
