// Logisim project level triggered D type flip flop.circ as structural Verilog: 1 circuit, main circuit main
// L D-type FF
module main (
  input  Clock,
  input  Data,
  output Q,
  output Q_bar
);

  wire and_1_out, and_2_out, not_1_out;

  not not_1 (not_1_out, Data);
  and and_1 (and_1_out, not_1_out, Clock);
  and and_2 (and_2_out, Clock, Data);
  nor nor_1 (Q, and_1_out, Q_bar);
  nor nor_2 (Q_bar, Q, and_2_out);
endmodule
